// Logisim project ALU8.circ as structural Verilog: 6 circuits, main circuit FULLADDER8
module main (
  input  [7:0] X,
  input  in_2,
  input  [7:0] Y,
  input  [1:0] opcode,
  input  in_5,
  input  in_6,
  output EQ,
  output CF,
  output ZF,
  output [7:0] RESULT,
  output SF,
  output out_12,
  output OVF
);

  wire or_2_out, or_3_out, or_4_out, or_5_out, or_6_out, or_7_out, or_8_out, or_9_out, xor_1_out, xor_2_out;
  wire [2:0] bit_extender_1_out;
  wire [7:0] and_1_out, fulladder8_1_out_4, or_1_out, right_1_result;

  Bit_Extender #(.out_width(3)) bit_extender_1 (.in(Y), .out(bit_extender_1_out));
  assign or_1_out = X | Y;  // OR_Gate or_1, 8 bits wide
  assign and_1_out = X & Y;  // AND_Gate and_1, 8 bits wide
  Multiplexer multiplexer_1 (.in0(out_12), .in1(in_6), .out(OVF), .sel(CF));
  xor xor_1 (xor_1_out, X[7], Y[7]);
  customComparator customcomparator_1 (.X(X), .Y(Y), .EQUAL(EQ));
  FULLADDER8 fulladder8_1 (.in_1(in_2), .X(X), .Y(Y), .out_4(fulladder8_1_out_4), .out_5(CF));
  right right_1 (.X(X), .Y(bit_extender_1_out), .RESULT(right_1_result));
  xor xor_2 (xor_2_out, RESULT[7], or_2_out);
  Multiplexer #(.select(2), .width(8)) multiplexer_2 (
    .in0(fulladder8_1_out_4), .in1(or_1_out), .in2(and_1_out), .in3(right_1_result), .out(RESULT),
    .sel(opcode));
  Multiplexer multiplexer_3 (.in0(xor_2_out), .in1(in_5), .out(out_12), .sel(xor_1_out));
  or or_2 (or_2_out, X[7], Y[7]);
  or or_3 (or_3_out, RESULT[0], RESULT[1]);
  or or_4 (or_4_out, or_3_out, RESULT[2]);
  or or_5 (or_5_out, or_4_out, RESULT[3]);
  or or_6 (or_6_out, or_5_out, RESULT[4]);
  or or_7 (or_7_out, or_6_out, RESULT[5]);
  or or_8 (or_8_out, or_7_out, RESULT[6]);
  or or_9 (or_9_out, or_8_out, RESULT[7]);
  not not_1 (ZF, or_9_out);

  assign SF = RESULT[7];

  // Other names for the same wires on the sheet: a[7:0] = X; D = X[7]; b[7:0] = Y; F = CF; G = out_12
endmodule

module FULLADDER8 (
  input  in_1,
  input  [7:0] X,
  input  [7:0] Y,
  output [7:0] out_4,
  output out_5
);

  wire fulladder_1_cout, fulladder_2_cout, fulladder_3_cout, fulladder_4_cout, fulladder_5_cout,
       fulladder_6_cout, fulladder_7_cout;

  fulladder fulladder_1 (.in_1(X[0]), .in_2(Y[0]), .CIN(in_1), .SUM(out_4[0]), .Cout(fulladder_1_cout));
  fulladder fulladder_2 (.in_1(X[1]), .in_2(Y[1]), .CIN(fulladder_1_cout), .SUM(out_4[1]), .Cout(fulladder_2_cout));
  fulladder fulladder_3 (.in_1(X[2]), .in_2(Y[2]), .CIN(fulladder_2_cout), .SUM(out_4[2]), .Cout(fulladder_3_cout));
  fulladder fulladder_4 (.in_1(X[3]), .in_2(Y[3]), .CIN(fulladder_3_cout), .SUM(out_4[3]), .Cout(fulladder_4_cout));
  fulladder fulladder_5 (.in_1(X[4]), .in_2(Y[4]), .CIN(fulladder_4_cout), .SUM(out_4[4]), .Cout(fulladder_5_cout));
  fulladder fulladder_6 (.in_1(X[5]), .in_2(Y[5]), .CIN(fulladder_5_cout), .SUM(out_4[5]), .Cout(fulladder_6_cout));
  fulladder fulladder_7 (.in_1(X[6]), .in_2(Y[6]), .CIN(fulladder_6_cout), .SUM(out_4[6]), .Cout(fulladder_7_cout));
  fulladder fulladder_8 (.in_1(X[7]), .in_2(Y[7]), .CIN(fulladder_7_cout), .SUM(out_4[7]), .Cout(out_5));
endmodule

module customComparator (
  input  [7:0] X,
  input  [7:0] Y,
  output EQUAL
);

  wire xnor_1_out, xnor_2_out, xnor_3_out, xnor_4_out, xnor_5_out, xnor_6_out, xnor_7_out, xnor_8_out;

  xnor xnor_1 (xnor_1_out, X[0], Y[0]);
  xnor xnor_2 (xnor_2_out, X[1], Y[1]);
  xnor xnor_3 (xnor_3_out, X[2], Y[2]);
  xnor xnor_4 (xnor_4_out, X[3], Y[3]);
  xnor xnor_5 (xnor_5_out, X[4], Y[4]);
  xnor xnor_6 (xnor_6_out, Y[5], X[5]);
  xnor xnor_7 (xnor_7_out, X[6], Y[6]);
  xnor xnor_8 (xnor_8_out, X[7], Y[7]);
  and and_1 (EQUAL, xnor_1_out, xnor_2_out, xnor_3_out, xnor_4_out, xnor_5_out, xnor_6_out, xnor_7_out, xnor_8_out);
endmodule

module rotl (
  input  [7:0] X,
  input  [2:0] Y,
  output [7:0] out_3
);

  Multiplexer #(.select(3)) multiplexer_1 (
    .in0(X[7]), .in1(X[6]), .in2(X[5]), .in3(X[4]), .in4(X[3]), .in5(X[2]), .in6(X[1]), .in7(X[0]),
    .out(out_3[7]), .sel(Y));
  Multiplexer #(.select(3)) multiplexer_2 (
    .in0(X[6]), .in1(X[5]), .in2(X[4]), .in3(X[3]), .in4(X[2]), .in5(X[1]), .in6(X[0]), .in7(X[7]),
    .out(out_3[6]), .sel(Y));
  Multiplexer #(.select(3)) multiplexer_3 (
    .in0(X[5]), .in1(X[4]), .in2(X[3]), .in3(X[2]), .in4(X[1]), .in5(X[0]), .in6(X[7]), .in7(X[6]),
    .out(out_3[5]), .sel(Y));
  Multiplexer #(.select(3)) multiplexer_4 (
    .in0(X[4]), .in1(X[3]), .in2(X[2]), .in3(X[1]), .in4(X[0]), .in5(X[7]), .in6(X[6]), .in7(X[5]),
    .out(out_3[4]), .sel(Y));
  Multiplexer #(.select(3)) multiplexer_5 (
    .in0(X[3]), .in1(X[2]), .in2(X[1]), .in3(X[0]), .in4(X[7]), .in5(X[6]), .in6(X[5]), .in7(X[4]),
    .out(out_3[3]), .sel(Y));
  Multiplexer #(.select(3)) multiplexer_6 (
    .in0(X[2]), .in1(X[1]), .in2(X[0]), .in3(X[7]), .in4(X[6]), .in5(X[5]), .in6(X[4]), .in7(X[3]),
    .out(out_3[2]), .sel(Y));
  Multiplexer #(.select(3)) multiplexer_7 (
    .in0(X[1]), .in1(X[0]), .in2(X[7]), .in3(X[6]), .in4(X[5]), .in5(X[4]), .in6(X[3]), .in7(X[2]),
    .out(out_3[1]), .sel(Y));
  Multiplexer #(.select(3)) multiplexer_8 (
    .in0(X[0]), .in1(X[7]), .in2(X[6]), .in3(X[5]), .in4(X[4]), .in5(X[3]), .in6(X[2]), .in7(X[1]),
    .out(out_3[0]), .sel(Y));
endmodule

module fulladder (
  input  in_1,
  input  in_2,
  input  CIN,
  output SUM,
  output Cout
);

  wire and_1_out, and_2_out, xor_1_out;

  xor xor_1 (xor_1_out, in_1, in_2);
  xor xor_2 (SUM, xor_1_out, CIN);
  and and_1 (and_1_out, xor_1_out, CIN);
  and and_2 (and_2_out, in_1, in_2);
  or or_1 (Cout, and_1_out, and_2_out);
endmodule

module right (
  input  [7:0] X,
  input  [2:0] Y,
  output [7:0] RESULT
);

  Multiplexer #(.select(3)) multiplexer_1 (
    .in0(X[7]), .in1(X[0]), .in2(X[1]), .in3(X[2]), .in4(X[3]), .in5(X[4]), .in6(X[5]), .in7(X[6]),
    .out(RESULT[7]), .sel(Y));
  Multiplexer #(.select(3)) multiplexer_2 (
    .in0(X[6]), .in1(X[7]), .in2(X[0]), .in3(X[1]), .in4(X[2]), .in5(X[3]), .in6(X[4]), .in7(X[5]),
    .out(RESULT[6]), .sel(Y));
  Multiplexer #(.select(3)) multiplexer_3 (
    .in0(X[5]), .in1(X[6]), .in2(X[7]), .in3(X[0]), .in4(X[1]), .in5(X[2]), .in6(X[3]), .in7(X[4]),
    .out(RESULT[5]), .sel(Y));
  Multiplexer #(.select(3)) multiplexer_4 (
    .in0(X[4]), .in1(X[5]), .in2(X[6]), .in3(X[7]), .in4(X[0]), .in5(X[1]), .in6(X[2]), .in7(X[3]),
    .out(RESULT[4]), .sel(Y));
  Multiplexer #(.select(3)) multiplexer_5 (
    .in0(X[3]), .in1(X[4]), .in2(X[5]), .in3(X[6]), .in4(X[7]), .in5(X[0]), .in6(X[1]), .in7(X[2]),
    .out(RESULT[3]), .sel(Y));
  Multiplexer #(.select(3)) multiplexer_6 (
    .in0(X[2]), .in1(X[3]), .in2(X[4]), .in3(X[5]), .in4(X[6]), .in5(X[7]), .in6(X[0]), .in7(X[1]),
    .out(RESULT[2]), .sel(Y));
  Multiplexer #(.select(3)) multiplexer_7 (
    .in0(X[1]), .in1(X[2]), .in2(X[3]), .in3(X[4]), .in4(X[5]), .in5(X[6]), .in6(X[7]), .in7(X[0]),
    .out(RESULT[1]), .sel(Y));
  Multiplexer #(.select(3)) multiplexer_8 (
    .in0(X[0]), .in1(X[1]), .in2(X[2]), .in3(X[3]), .in4(X[4]), .in5(X[5]), .in6(X[6]), .in7(X[7]),
    .out(RESULT[0]), .sel(Y));
endmodule
