// Logisim project cng331projepartfafu.circ as structural Verilog: 7 circuits, main circuit ALU8
// ALU
module ALU8 (
  input  [7:0] X,
  input  [7:0] Y,
  input  [2:0] ALUfunc,
  output flag,
  output [7:0] RESULT
);

  wire comparator_1_lt;
  wire [7:0] adder_1_out, and_1_out, bit_extender_1_out, or_1_out, shifter_1_out;

  Comparator comparator_1 (.a(X), .b(Y), .eq(flag), .lt(comparator_1_lt));  // open: gt
  Adder adder_1 (.a(X), .b(Y), .out(adder_1_out));  // open: cin, cout
  Shifter #(.shift("rl")) shifter_1 (.in(X), .\dist (Y[2:0]), .out(shifter_1_out));
  assign and_1_out = X & Y;  // AND_Gate and_1, 8 bits wide
  assign or_1_out = X | Y;  // OR_Gate or_1, 8 bits wide
  assign bit_extender_1_out = {{7{1'b0}}, comparator_1_lt};  // Bit_Extender bit_extender_1
  Multiplexer #(.enable("true"), .select(3), .width(8)) multiplexer_1 (
    .in0(adder_1_out), .in1(and_1_out), .in2(or_1_out), .in3(shifter_1_out), .in4(bit_extender_1_out),
    .out(RESULT), .sel(ALUfunc));  // open: in5, in6, in7, en
endmodule

module ROMcurcit (
  input  [9:0] in_1,
  output [20:0] out_2
);

  ROM #(.addrWidth(10), .dataWidth(21), .misaligned("true")) rom_1 (.addr(in_1), .data(out_2));

  // Notes on the sheet:
  //   contents of rom_1 (hex, n*v repeats v):
  //   0 60307 60502 1c0009 1ee100 60403 e600 20201 eb006 18ec00 42001 1bc000 8d600 bf002 16000c 43004
endmodule

module Ramcurcit (
  input  [7:0] Address,
  input  write,
  input  read,
  input  clock,
  input  [7:0] data,
  output [7:0] out_6
);

  RAM #(.asyncread("true"), .trigger("falling")) ram_1 (
    .addr(Address), .we(write), .oe(read), .clk(clock), .din(data), .dout(out_6));
endmodule

module maincircuit (
  input  in_1,
  output [9:0] out_2,
  output [7:0] out_3,
  output [2:0] out_4
);

  wire clock_1_out, controlunit_1_branch, controlunit_1_jalflag, controlunit_1_mux2, controlunit_1_mw,
       controlunit_1_we, controlunit_1_wr, E;
  wire [1:0] and_1_out, bit_extender_1_out, controlunit_1_mux10, controlunit_1_pc;
  wire [2:0] controlunit_1_alufunc0, controlunit_1_ra;
  wire [7:0] adder_2_out, alu8_1_result, bit_extender_2_out, main_1_rsout, main_1_rtout, multiplexer_4_out,
       ramcurcit_1_out_6;
  wire [9:0] adder_1_out, B, bit_extender_3_out, multiplexer_1_out, R, S;
  wire [20:0] romcurcit_1_out_2;
  wire [23:10] bit_extender_3_out_2;

  Clock clock_1 (.out(clock_1_out));
  assign and_1_out = controlunit_1_pc & bit_extender_1_out;  // AND_Gate and_1, 2 bits wide
  Multiplexer #(.select(2), .width(10)) multiplexer_1 (
    .in0(adder_1_out), .in1(S), .in2(bit_extender_3_out), .in3(R), .out(multiplexer_1_out), .sel(and_1_out));
  pc pc_1 (.data(multiplexer_1_out), .clock(clock_1_out), .reset(in_1), .out_4(out_2));
  Adder #(.width(10)) adder_1 (.a(10'h1), .b(out_2), .out(adder_1_out));  // open: cin, cout
  assign bit_extender_1_out = {{1{controlunit_1_branch}}, controlunit_1_branch};  // Bit_Extender bit_extender_1
  Bit_Extender #(.in_width(10), .out_width(8)) bit_extender_2 (.in(out_2), .out(bit_extender_2_out));
  Adder adder_2 (.a(bit_extender_2_out), .b(8'h1), .out(adder_2_out));  // open: cin, cout
  assign {bit_extender_3_out_2, bit_extender_3_out} = {{3{romcurcit_1_out_2[20]}}, romcurcit_1_out_2};  // Bit_Extender bit_extender_3
  Adder #(.width(10)) adder_3 (.a(out_2), .b(B), .out(S));  // open: cin, cout
  assign B = {{2{bit_extender_3_out[7]}}, bit_extender_3_out[7:0]};  // Bit_Extender bit_extender_4
  ROMcurcit romcurcit_1 (.in_1(out_2), .out_2(romcurcit_1_out_2));
  assign R = {{2{main_1_rsout[7]}}, main_1_rsout};  // Bit_Extender bit_extender_5
  Multiplexer #(.select(2), .width(8)) multiplexer_2 (
    .in0(alu8_1_result), .in1(ramcurcit_1_out_6), .in2(bit_extender_3_out[7:0]), .in3(adder_2_out),
    .out(out_3), .sel(controlunit_1_mux10));
  ControlUnit controlunit_1 (
    .opcode0(bit_extender_3_out_2[17]), .opcode1(bit_extender_3_out_2[18]),
    .opcode2(bit_extender_3_out_2[19]), .opcode3(bit_extender_3_out_2[20]), .E(E),
    .mux10(controlunit_1_mux10[0]), .mux11(controlunit_1_mux10[1]), .mux2(controlunit_1_mux2),
    .WE(controlunit_1_we), .MW(controlunit_1_mw), .WR(controlunit_1_wr),
    .Alufunc0(controlunit_1_alufunc0[0]), .Alufunc1(controlunit_1_alufunc0[1]),
    .jalflag(controlunit_1_jalflag), .BRANCH(controlunit_1_branch), .PC(controlunit_1_pc),
    .Alufunc3(controlunit_1_alufunc0[2]), .Ra(controlunit_1_ra));
  Multiplexer #(.width(3)) multiplexer_3 (
    .in0({bit_extender_3_out_2[10], bit_extender_3_out[9:8]}), .in1(controlunit_1_ra), .out(out_4),
    .sel(controlunit_1_jalflag));
  Multiplexer #(.width(8)) multiplexer_4 (
    .in0(main_1_rtout), .in1(bit_extender_3_out[7:0]), .out(multiplexer_4_out), .sel(controlunit_1_mux2));
  main main_1 (
    .WE(controlunit_1_we), .rd(out_4), .data(out_3), .clock(clock_1_out), .rt(bit_extender_3_out_2[13:11]),
    .rs(bit_extender_3_out_2[16:14]), .RTOUT(main_1_rtout), .RSOUT(main_1_rsout));
  ALU8 alu8_1 (
    .X(main_1_rsout), .Y(multiplexer_4_out), .ALUfunc(controlunit_1_alufunc0), .flag(E),
    .RESULT(alu8_1_result));
  Ramcurcit ramcurcit_1 (
    .Address(alu8_1_result), .write(controlunit_1_mw), .read(controlunit_1_wr), .clock(clock_1_out),
    .data(main_1_rtout), .out_6(ramcurcit_1_out_6));

  // Other names for the same wires on the sheet: A[7:0] = out_3
endmodule

module main (
  input  WE,
  input  [2:0] rd,
  input  [7:0] data,
  input  clock,
  input  [2:0] rt,
  input  [2:0] rs,
  output [7:0] RTOUT,
  output [7:0] RSOUT
);

  wire decoder_1_out0, decoder_1_out1, decoder_1_out2, decoder_1_out3, decoder_1_out4, decoder_1_out5,
       decoder_1_out6, decoder_1_out7;
  wire [7:0] register_1_q, register_2_q, register_3_q, register_4_q, register_5_q, register_6_q,
       register_7_q, register_8_q;

  Decoder #(.select(3)) decoder_1 (
    .out0(decoder_1_out0), .out1(decoder_1_out1), .out2(decoder_1_out2), .out3(decoder_1_out3),
    .out4(decoder_1_out4), .out5(decoder_1_out5), .out6(decoder_1_out6), .out7(decoder_1_out7), .sel(rd),
    .en(WE));
  Multiplexer #(.select(3), .width(8)) multiplexer_1 (
    .in0(register_1_q), .in1(register_2_q), .in2(register_3_q), .in3(register_4_q), .in4(register_5_q),
    .in5(register_6_q), .in6(register_7_q), .in7(register_8_q), .out(RTOUT), .sel(rt));
  Multiplexer #(.select(3), .width(8)) multiplexer_2 (
    .in0(register_1_q), .in1(register_2_q), .in2(register_3_q), .in3(register_4_q), .in4(register_5_q),
    .in5(register_6_q), .in6(register_7_q), .in7(register_8_q), .out(RSOUT), .sel(rs));
  Register #(.trigger("falling")) register_1 (
    .D(data), .en(decoder_1_out0), .clk(clock), .Q(register_1_q));  // open: clr
  Register #(.trigger("falling")) register_2 (
    .D(data), .en(decoder_1_out1), .clk(clock), .Q(register_2_q));  // open: clr
  Register #(.trigger("falling")) register_3 (
    .D(data), .en(decoder_1_out2), .clk(clock), .Q(register_3_q));  // open: clr
  Register #(.trigger("falling")) register_4 (
    .D(data), .en(decoder_1_out3), .clk(clock), .Q(register_4_q));  // open: clr
  Register #(.trigger("falling")) register_5 (
    .D(data), .en(decoder_1_out4), .clk(clock), .Q(register_5_q));  // open: clr
  Register #(.trigger("falling")) register_6 (
    .D(data), .en(decoder_1_out5), .clk(clock), .Q(register_6_q));  // open: clr
  Register #(.trigger("falling")) register_7 (
    .D(data), .en(decoder_1_out6), .clk(clock), .Q(register_7_q));  // open: clr
  Register #(.trigger("falling")) register_8 (
    .D(data), .en(decoder_1_out7), .clk(clock), .Q(register_8_q));  // open: clr
endmodule

module ControlUnit (
  input  opcode0,
  input  opcode1,
  input  opcode2,
  input  opcode3,
  input  E,
  output mux10,
  output mux11,
  output mux2,
  output WE,
  output MW,
  output WR,
  output Alufunc0,
  output Alufunc1,
  output jalflag,
  output BRANCH,
  output [1:0] PC,
  output Alufunc3,
  output [2:0] Ra
);

  wire and_1_out, and_2_out, and_3_out, and_4_out, and_5_out, and_6_out, and_7_out, and_8_out, and_9_out,
       and_10_out, and_11_out, and_12_out, and_13_out, and_14_out, and_19_out, and_20_out, and_21_out,
       and_22_out, and_23_out, not_1_out, not_2_out, not_3_out, not_4_out, not_5_out, not_6_out, not_7_out,
       not_8_out, not_9_out, not_10_out, not_11_out, not_12_out, not_13_out, not_14_out, not_15_out,
       not_16_out, not_17_out, not_18_out, not_19_out, not_20_out, not_21_out, not_22_out, not_23_out,
       not_24_out, not_25_out, not_26_out, not_27_out, not_28_out, not_29_out, not_30_out, not_31_out,
       not_32_out, not_33_out, not_34_out, not_35_out;

  not not_1 (not_1_out, opcode1);
  not not_2 (not_2_out, opcode3);
  not not_3 (not_3_out, E);
  not not_4 (not_4_out, opcode2);
  not not_5 (not_5_out, opcode1);
  not not_6 (not_6_out, opcode0);
  not not_7 (not_7_out, opcode3);
  not not_8 (not_8_out, opcode1);
  not not_9 (not_9_out, opcode2);
  not not_10 (not_10_out, opcode1);
  not not_11 (not_11_out, opcode3);
  not not_12 (not_12_out, opcode0);
  not not_13 (not_13_out, opcode1);
  not not_14 (not_14_out, opcode0);
  not not_15 (not_15_out, opcode2);
  not not_16 (not_16_out, opcode3);
  not not_17 (not_17_out, opcode2);
  not not_18 (not_18_out, opcode3);
  not not_19 (not_19_out, opcode1);
  not not_20 (not_20_out, opcode2);
  not not_21 (not_21_out, opcode3);
  and and_1 (and_1_out, opcode0, not_1_out, opcode2, E);
  and and_2 (and_2_out, opcode0, opcode1, not_4_out, opcode3);
  and and_3 (and_3_out, opcode0, not_5_out, opcode2, opcode3);
  and and_4 (and_4_out, not_6_out, opcode1, opcode2, opcode3);
  and and_5 (and_5_out, not_7_out, opcode2, opcode0);
  and and_6 (and_6_out, opcode2, not_8_out, opcode0);
  and and_7 (and_7_out, opcode0, not_10_out, not_11_out);
  and and_8 (and_8_out, not_12_out, opcode1, opcode2, opcode3);
  and and_9 (and_9_out, opcode1, not_17_out, not_18_out);
  not not_22 (not_22_out, opcode0);
  and and_10 (and_10_out, opcode0, opcode1, not_2_out, opcode2, not_3_out);
  and and_11 (and_11_out, opcode0, opcode1, not_9_out, opcode3);
  and and_12 (and_12_out, opcode0, not_13_out, opcode2, opcode3);
  and and_13 (and_13_out, not_14_out, opcode1, opcode2, opcode3);
  not not_23 (not_23_out, opcode0);
  and and_14 (and_14_out, opcode0, not_15_out, not_16_out);
  not not_24 (not_24_out, opcode0);
  not not_25 (not_25_out, opcode2);
  not not_26 (not_26_out, opcode3);
  and and_15 (WR, opcode0, not_19_out, not_20_out, not_21_out);
  not not_27 (not_27_out, opcode1);
  or or_1 (mux10, and_7_out, and_8_out);
  not not_28 (not_28_out, opcode2);
  not not_29 (not_29_out, opcode3);
  not not_30 (not_30_out, opcode0);
  not not_31 (not_31_out, opcode1);
  not not_32 (not_32_out, opcode2);
  not not_33 (not_33_out, opcode3);
  and and_16 (Alufunc0, opcode2, not_27_out);
  not not_34 (not_34_out, opcode0);
  not not_35 (not_35_out, opcode1);
  and and_17 (jalflag, not_22_out, opcode1, opcode2, opcode3);
  or or_2 (BRANCH, and_1_out, and_10_out, and_2_out, and_3_out, and_4_out);
  or or_3 (PC[0], and_5_out, and_6_out);
  and and_18 (Alufunc3, opcode1, opcode2, opcode3);
  and and_19 (and_19_out, opcode1, not_28_out, not_29_out);
  and and_20 (and_20_out, not_23_out, opcode1, opcode2, opcode3);
  or or_4 (mux2, and_14_out, and_9_out);
  and and_21 (and_21_out, not_30_out, not_31_out);
  and and_22 (and_22_out, opcode0, not_32_out, not_33_out);
  and and_23 (and_23_out, opcode1, opcode2, opcode3);
  and and_24 (Alufunc1, not_34_out, not_35_out, opcode3);
  or or_5 (PC[1], and_11_out, and_12_out, and_13_out);
  or or_6 (WE, and_21_out, and_22_out, and_23_out);
  and and_25 (MW, not_24_out, opcode1, not_25_out, not_26_out);
  or or_7 (mux11, and_19_out, and_20_out);

  assign Ra = 3'b111;

  // Other names for the same wires on the sheet: A = opcode0; B = opcode1; C = opcode2; D = opcode3
endmodule

module pc (
  input  [9:0] data,
  input  clock,
  input  reset,
  output [9:0] out_4
);

  Counter #(.max('h3ff), .ongoal("load"), .width(10)) counter_1 (
    .load(1'b1), .D(data), .count(1'b1), .Q(out_4), .up(1'b0), .clk(clock), .clr(reset));  // open: carry

  // Notes on the sheet:
  //   data: initial=0x1
endmodule
